# Fritzing sketch ProjetoAutoHome_Fritzing (saved by Fritzing 0.9.3b)
breadboards: 2

parts:
  YwRobot_Power_Supply1 = YwRobot Breadboard Power Supply [part_number=545043]
  DHT1 = DHT11 Humitidy and Temperature Sensor
  Part1 = KY-022 Infrared Receiver Module [package="Breakout board"]
  U2 = 74HC595 [package="DIP16 [THT]"]
  Componente1 = LCD1602-I2C
  U3 = NodeMCU V3.0
  U4 = 74HC595 [package="DIP16 [THT]"]
  R14 = Resistor [tolerance=±5% resistance=10k package="2512 [SMD]"]
  R15 = Resistor [tolerance=±5% resistance=220 package="0402 [SMD]"]
  R16 = Resistor [tolerance=±5% resistance=220 package="0402 [SMD]"]
  R17 = Resistor [tolerance=±5% resistance=220 package="0402 [SMD]"]
  R18 = Resistor [tolerance=±5% resistance=220 package="0402 [SMD]"]
  R19 = Resistor [tolerance=±5% resistance=220 package="0402 [SMD]"]
  R20 = Resistor [tolerance=±5% resistance=220 package="0402 [SMD]"]
  R21 = Resistor [tolerance=±5% resistance=220 package="0402 [SMD]"]
  R22 = Resistor [tolerance=±5% resistance=220 package="0402 [SMD]"]
  D1 = Rectifier Diode [package="Melf DO-213 AA [SMD]"]  # not connected
  R23 = Resistor [tolerance=±5% resistance=10k package="0402 [SMD]"]
  R24 = Resistor [tolerance=±5% resistance=10k package="0402 [SMD]"]
  R25 = Resistor [tolerance=±5% resistance=10k package="0402 [SMD]"]
  R26 = Resistor [tolerance=±5% resistance=10k package="0402 [SMD]"]
  R27 = Resistor [tolerance=±5% resistance=10k package="0402 [SMD]"]
  R28 = Resistor [tolerance=±5% resistance=10k package="0402 [SMD]"]
  R29 = Resistor [tolerance=±5% resistance=10k package="0402 [SMD]"]
  R30 = Resistor [tolerance=±5% resistance=10k package="0402 [SMD]"]
  LED9 = LED - 3mm [color="Red (633nm)" package="3 mm [THT]"]
  LED1 = LED - 5mm [color="White (4500K)" package="5 mm [THT]"]
  LED2 = LED - 5mm [color="White (4500K)" package="5 mm [THT]"]
  LED3 = LED - 5mm [color="White (4500K)" package="5 mm [THT]"]
  LED4 = LED - 5mm [color="White (4500K)" package="5 mm [THT]"]
  LED5 = LED - 5mm [color="White (4500K)" package="5 mm [THT]"]
  LED7 = LED - 5mm [color="White (4500K)" package="5 mm [THT]"]
  LED8 = LED - 5mm [color="White (4500K)" package="5 mm [THT]"]
  LED6 = LED - 5mm [color="White (4500K)" package="5 mm [THT]"]
  LED10 = LED - 3mm [color="Green (555nm)" package="3 mm [THT]"]
  R31 = Resistor [tolerance=±5% resistance=330 package="0402 [SMD]"]
  R32 = Resistor [tolerance=±5% resistance=330 package="0402 [SMD]"]
  S18 = Momentary Switch [package=ksa_sealed_tac_switch]
  S19 = Momentary Switch [package=ksa_sealed_tac_switch]
  S20 = Momentary Switch [package=ksa_sealed_tac_switch]
  S21 = Momentary Switch [package=ksa_sealed_tac_switch]
  S22 = Momentary Switch [package=ksa_sealed_tac_switch]
  S23 = Momentary Switch [package=ksa_sealed_tac_switch]
  S24 = Momentary Switch [package=ksa_sealed_tac_switch]
  S25 = Momentary Switch [package=ksa_sealed_tac_switch]

nets:
  N1: YwRobot_Power_Supply1.VCC#5, YwRobot_Power_Supply1.VCC#6, R23.Pin_0, R24.Pin_0, R25.Pin_0, R26.Pin_0, R27.Pin_0, R28.Pin_0, R29.Pin_0, R30.Pin_0
  VCC: YwRobot_Power_Supply1.VCC#9, YwRobot_Power_Supply1.VCC#10, DHT1.VDD, Part1.Vin, U2.MR, U2.VCC, U4.MR, U4.VCC, R14.Pin_1, R15.Pin_0, R16.Pin_0, R17.Pin_0, R18.Pin_0, R19.Pin_0, R20.Pin_0, R21.Pin_0, R22.Pin_0
  N2: YwRobot_Power_Supply1.GND#11, YwRobot_Power_Supply1.GND#12, U2.GND
  GND: YwRobot_Power_Supply1.GND#13, YwRobot_Power_Supply1.GND#14, DHT1.GND, Part1.-, U2.OE, U3.GND#6, U3.GND#13, U3.GND#16, U3.GND#33, U4.GND, U4.OE, R31.Pin_0, R32.Pin_0
  N3: DHT1.DATA, U3.D6, R14.Pin_0
  N4: U2.Q1, S24.1, S24.2
  N5: U2.Q2, S23.1, S23.2
  N6: U2.Q3, S22.1, S22.2
  N7: U2.Q4, S21.1, S21.2
  N8: U2.Q5, S20.1, S20.2
  N9: U2.Q6, S19.1, S19.2
  N10: U2.Q7, S18.1, S18.2
  N11: U2.Q7', U4.DS
  N12: U2.SH_CP, U3.D5, U4.SH_CP
  N13: U2.ST_CP, U3.D8, U4.ST_CP
  N14: U2.DS, U3.D7
  N15: U2.Q0, S25.1, S25.2
  N16: Componente1.GND, U3.GND#41
  N17: Componente1.VCC, U3.VU
  N18: Componente1.SDA, U3.D2
  N19: Componente1.SCL, U3.D1
  N20: U3.D0, LED9.anode
  N21: U3.D3, LED10.anode
  N22: U3.A0, R23.Pin_1, R24.Pin_1, R25.Pin_1, R26.Pin_1, R27.Pin_1, R28.Pin_1, R29.Pin_1, R30.Pin_1, S18.3, S18.4, S19.3, S19.4, S20.3, S20.4, S21.3, S21.4, S22.3, S22.4, S23.3, S23.4, S24.3, S24.4, S25.3, S25.4
  N23: U4.Q1, LED2.cathode
  N24: U4.Q2, LED3.cathode
  N25: U4.Q3, LED4.cathode
  N26: U4.Q4, LED5.cathode
  N27: U4.Q5, LED6.cathode
  N28: U4.Q6, LED7.cathode
  N29: U4.Q7, LED8.cathode
  N30: U4.Q0, LED1.cathode
  N31: R15.Pin_1, LED1.anode
  N32: R16.Pin_1, LED3.anode
  N33: R17.Pin_1, LED2.anode
  N34: R18.Pin_1, LED4.anode
  N35: R19.Pin_1, LED5.anode
  N36: R20.Pin_1, LED6.anode
  N37: R21.Pin_1, LED7.anode
  N38: R22.Pin_1, LED8.anode
  N39: LED9.cathode, R31.Pin_1
  N40: LED10.cathode, R32.Pin_1

notes:
  3.3v
  v 2.2.4.0

custom parts:
  YwRobot Breadboard Power Supply: The YwRobot Breadboard Power Supply (MB-V2) has two power rails; they can be 5V or 3V3. Power to the module can be provided through the female USB socket or through the A10 (female) 2.1mm power jack.
  DHT11 Humitidy and Temperature Sensor: DHT11 Humidity and Temperature Sensor
  KY-022 Infrared Receiver Module: Arduino IR receiver module KY-022, reacts to 38kHz infrared light.
  LCD1602-I2C: A standard character display, usually with 2x16 characters. Comes in many colors with LCM1602 IIC attached.
  NodeMCU V3.0: ESP8266 based NodeMCU
